// Logisim project Main.circ as structural Verilog
module XOR_Gate (
  input  A,
  input  B,
  output Out
);

  wire and_1_out, and_2_out, not_1_out, not_2_out;

  and and_1 (and_1_out, A, not_1_out);
  not not_1 (not_1_out, B);
  not not_2 (not_2_out, A);
  and and_2 (and_2_out, not_2_out, B);
  or or_1 (Out, and_1_out, and_2_out);
endmodule

module Half_Adder (
  input  A,
  input  B,
  output Sum,
  output Cout
);

  XOR_Gate xor_1 (.A(A), .B(B), .Out(Sum));
  and and_1 (Cout, A, B);
endmodule

module Full_Adder (
  input  A,
  input  B,
  input  Cin,
  output Sum,
  output Cout
);

  wire half_adder_1_cout, half_adder_1_sum, half_adder_2_cout;

  Half_Adder half_adder_1 (.A(A), .B(B), .Sum(half_adder_1_sum), .Cout(half_adder_1_cout));
  Half_Adder half_adder_2 (.A(half_adder_1_sum), .B(Cin), .Sum(Sum), .Cout(half_adder_2_cout));
  or or_1 (Cout, half_adder_2_cout, half_adder_1_cout);
endmodule

module _2_Mux (
  input  A,
  input  B,
  input  Select,
  output Out
);

  wire and_1_out, and_2_out, not_1_out;

  and and_1 (and_1_out, A, not_1_out);
  not not_1 (not_1_out, Select);
  and and_2 (and_2_out, B, Select);
  or or_1 (Out, and_1_out, and_2_out);
endmodule

module _4_Mux (
  input  A,
  input  B,
  input  C,
  input  D,
  input  S0,
  input  S1,
  output Out
);

  wire n2_mux_1_out, n2_mux_2_out;

  _2_Mux u_2_mux_1 (.A(A), .B(B), .Select(S0), .Out(n2_mux_1_out));
  _2_Mux u_2_mux_2 (.A(C), .B(D), .Select(S0), .Out(n2_mux_2_out));
  _2_Mux u_2_mux_3 (.A(n2_mux_1_out), .B(n2_mux_2_out), .Select(S1), .Out(Out));
endmodule

module _1_bit_ALU (
  input  A,
  input  B,
  input  Cin,
  input  S1,
  input  S0,
  output Out,
  output Cout
);

  wire and_1_out, full_adder_1_sum, or_1_out;

  and and_1 (and_1_out, A, B);
  or or_1 (or_1_out, A, B);
  Full_Adder full_adder_1 (.A(A), .B(B), .Cin(Cin), .Sum(full_adder_1_sum), .Cout(Cout));
  _4_Mux u_4_mux_1 (.A(full_adder_1_sum), .B(and_1_out), .C(or_1_out), .S0(S0), .S1(S1), .Out(Out));  // open: D
endmodule

module _4_bit_ALU (
  input  Cin,
  input  S1,
  input  S0,
  input  [3:0] A,
  input  [3:0] B,
  output [3:0] Out,
  output Cout
);

  wire n1_bit_alu_1_cout, n1_bit_alu_2_cout, n1_bit_alu_3_cout;

  _1_bit_ALU u_1_bit_alu_1 (.A(A[0]), .B(B[0]), .Cin(Cin), .S1(S1), .S0(S0), .Out(Out[0]), .Cout(n1_bit_alu_1_cout));
  _1_bit_ALU u_1_bit_alu_2 (
    .A(A[1]), .B(B[1]), .Cin(n1_bit_alu_1_cout), .S1(S1), .S0(S0), .Out(Out[1]), .Cout(n1_bit_alu_2_cout));
  _1_bit_ALU u_1_bit_alu_3 (
    .A(A[2]), .B(B[2]), .Cin(n1_bit_alu_2_cout), .S1(S1), .S0(S0), .Out(Out[2]), .Cout(n1_bit_alu_3_cout));
  _1_bit_ALU u_1_bit_alu_4 (.A(A[3]), .B(B[3]), .Cin(n1_bit_alu_3_cout), .S1(S1), .S0(S0), .Out(Out[3]), .Cout(Cout));
endmodule

module Full_1_bit__4_opp_ALU (
  input  A,
  input  B,
  input  Cin,
  input  S1,
  input  S0,
  output Out,
  output Cout
);

  wire and_1_out, full_adder_1_cout, full_adder_1_sum, n1_bit_alu_1_cout, n1_bit_alu_1_out, not_1_out;

  not not_1 (not_1_out, B);
  _1_bit_ALU u_1_bit_alu_1 (
    .A(A), .B(B), .Cin(Cin), .S1(S1), .S0(S0), .Out(n1_bit_alu_1_out), .Cout(n1_bit_alu_1_cout));
  and and_1 (and_1_out, S1, S0);
  Full_Adder full_adder_1 (.A(A), .B(not_1_out), .Cin(and_1_out), .Sum(full_adder_1_sum), .Cout(full_adder_1_cout));
  _2_Mux u_2_mux_1 (.A(n1_bit_alu_1_out), .B(full_adder_1_sum), .Select(and_1_out), .Out(Out));
  _2_Mux u_2_mux_2 (.A(n1_bit_alu_1_cout), .B(full_adder_1_cout), .Select(and_1_out), .Out(Cout));
endmodule

module Full_4_bit__4_opp_ALU (
  input  S1,
  input  S0,
  input  [3:0] A,
  input  [3:0] B,
  output [3:0] out_5,
  output Cout
);

  wire and_1_out, full_1_bit_4_opp_alu_1_cout, full_1_bit_4_opp_alu_2_cout, full_1_bit_4_opp_alu_3_cout;

  and and_1 (and_1_out, S1, S0);
  Full_1_bit__4_opp_ALU full_1_bit_4_opp_alu_1 (
    .A(A[0]), .B(B[0]), .Cin(and_1_out), .S1(S1), .S0(S0), .Out(out_5[0]), .Cout(full_1_bit_4_opp_alu_1_cout));
  Full_1_bit__4_opp_ALU full_1_bit_4_opp_alu_2 (
    .A(A[1]), .B(B[1]), .Cin(full_1_bit_4_opp_alu_1_cout), .S1(S1), .S0(S0), .Out(out_5[1]),
    .Cout(full_1_bit_4_opp_alu_2_cout));
  Full_1_bit__4_opp_ALU full_1_bit_4_opp_alu_3 (
    .A(A[2]), .B(B[2]), .Cin(full_1_bit_4_opp_alu_2_cout), .S1(S1), .S0(S0), .Out(out_5[2]),
    .Cout(full_1_bit_4_opp_alu_3_cout));
  Full_1_bit__4_opp_ALU full_1_bit_4_opp_alu_4 (
    .A(A[3]), .B(B[3]), .Cin(full_1_bit_4_opp_alu_3_cout), .S1(S1), .S0(S0), .Out(out_5[3]), .Cout(Cout));
endmodule
