// Logisim project Lab 4 - memory.circ as structural Verilog
module _4_bit_ALU (
  input  [3:0] A,
  input  [3:0] B,
  input  [1:0] ALU_Op,
  output [3:0] ALU_Out
);

  wire and_1_out;
  wire [3:0] adder_1_out, and_2_out, multiplexer_1_out, not_1_out, or_1_out;

  Multiplexer #(.width(4), .enable("false")) multiplexer_1 (
    .in0(B), .in1(not_1_out), .out(multiplexer_1_out), .sel(and_1_out));
  assign not_1_out = ~B;  // NOT_Gate not_1, 4 bits wide
  and and_1 (and_1_out, ALU_Op[0], ALU_Op[1]);
  Adder #(.width(4)) adder_1 (.a(A), .b(multiplexer_1_out), .out(adder_1_out), .cin(and_1_out));  // open: cout
  assign and_2_out = multiplexer_1_out & A;  // AND_Gate and_2, 4 bits wide
  assign or_1_out = multiplexer_1_out | A;  // OR_Gate or_1, 4 bits wide
  Multiplexer #(.select(2), .width(4), .enable("false")) multiplexer_2 (
    .in0(adder_1_out), .in1(and_2_out), .in2(or_1_out), .in3(adder_1_out), .out(ALU_Out), .sel(ALU_Op));

  // Notes on the sheet:
  //   4 Bit ALU
  //   00 = ADD
  //   01 = AND
  //   10 = OR
  //   11 = SUB
  //   sub not B
  //   sub cin
  //   sub
endmodule

module _8x4_bit_Register_File (
  input  [3:0] Data_In,
  input  [2:0] Read_Addr_1,
  input  Write_Enable,
  input  [2:0] Write_Addr,
  input  [2:0] Read_Addr_2,
  input  Clock,
  output [3:0] Read_1_Data,
  output [3:0] Read_2_Data
);

  wire demultiplexer_1_out0, demultiplexer_1_out1, demultiplexer_1_out2, demultiplexer_1_out3,
       demultiplexer_1_out4, demultiplexer_1_out5, demultiplexer_1_out6, demultiplexer_1_out7;
  wire [3:0] register_1_q, register_2_q, register_3_q, register_4_q, register_5_q, register_6_q,
       register_7_q, register_8_q;

  Demultiplexer #(.select(3), .enable("false")) demultiplexer_1 (
    .out0(demultiplexer_1_out0), .out1(demultiplexer_1_out1), .out2(demultiplexer_1_out2),
    .out3(demultiplexer_1_out3), .out4(demultiplexer_1_out4), .out5(demultiplexer_1_out5),
    .out6(demultiplexer_1_out6), .out7(demultiplexer_1_out7), .in(Write_Enable), .sel(Write_Addr));
  Register #(.width(4)) register_1 (
    .D(Data_In), .en(demultiplexer_1_out0), .Q(register_1_q), .clk(Clock));  // open: clr
  Register #(.width(4)) register_2 (
    .D(Data_In), .en(demultiplexer_1_out1), .Q(register_2_q), .clk(Clock));  // open: clr
  Register #(.width(4)) register_3 (
    .D(Data_In), .en(demultiplexer_1_out2), .Q(register_3_q), .clk(Clock));  // open: clr
  Register #(.width(4)) register_4 (
    .D(Data_In), .en(demultiplexer_1_out3), .Q(register_4_q), .clk(Clock));  // open: clr
  Register #(.width(4)) register_5 (
    .D(Data_In), .en(demultiplexer_1_out4), .Q(register_5_q), .clk(Clock));  // open: clr
  Register #(.width(4)) register_6 (
    .D(Data_In), .en(demultiplexer_1_out5), .Q(register_6_q), .clk(Clock));  // open: clr
  Register #(.width(4)) register_7 (
    .D(Data_In), .en(demultiplexer_1_out6), .Q(register_7_q), .clk(Clock));  // open: clr
  Register #(.width(4)) register_8 (
    .D(Data_In), .en(demultiplexer_1_out7), .Q(register_8_q), .clk(Clock));  // open: clr
  Multiplexer #(.select(3), .width(4), .enable("false")) multiplexer_1 (
    .in0(register_1_q), .in1(register_2_q), .in2(register_3_q), .in3(register_4_q), .in4(register_5_q),
    .in5(register_6_q), .in6(register_7_q), .in7(register_8_q), .out(Read_1_Data), .sel(Read_Addr_1));
  Multiplexer #(.select(3), .width(4), .enable("false")) multiplexer_2 (
    .in0(register_1_q), .in1(register_2_q), .in2(register_3_q), .in3(register_4_q), .in4(register_5_q),
    .in5(register_6_q), .in6(register_7_q), .in7(register_8_q), .out(Read_2_Data), .sel(Read_Addr_2));

  // Notes on the sheet:
  //   8x4-bit Register File
  //   R0
  //   R1
  //   R2
  //   R3
  //   R4
  //   R5
  //   R6
  //   R7
endmodule

module ALU_REG_Instruction (
  input  [13:0] dest,
  input  CLK,
  output [3:0] ALU_Out
);

  wire [3:0] bit_extender_1_out, multiplexer_1_out, n8x4_bit_register_file_1_read_1_data,
       n8x4_bit_register_file_1_read_2_data;

  _8x4_bit_Register_File u_8x4_bit_register_file_1 (
    .Read_Addr_2(dest[2:0]), .Data_In(ALU_Out), .Read_1_Data(n8x4_bit_register_file_1_read_1_data),
    .Read_Addr_1(dest[5:3]), .Write_Enable(1'b1), .Write_Addr(dest[8:6]),
    .Read_2_Data(n8x4_bit_register_file_1_read_2_data), .Clock(CLK));
  assign bit_extender_1_out = {{1{dest[2]}}, dest[2:0]};  // Bit_Extender bit_extender_1
  Multiplexer #(.width(4), .enable("false")) multiplexer_1 (
    .in0(n8x4_bit_register_file_1_read_2_data), .in1(bit_extender_1_out), .out(multiplexer_1_out),
    .sel(dest[13]));
  _4_bit_ALU u_4_bit_alu_1 (
    .A(n8x4_bit_register_file_1_read_1_data), .ALU_Out(ALU_Out), .B(multiplexer_1_out), .ALU_Op(dest[10:9]));

  // Notes on the sheet:
  //   op
  //   SW
  //   R/I
  //   LW
  //   dest
  //   src2
  //   src1
  //   src2
  //   dest
  //   src1
  //   immed data
  //   immed select
  //   ALU op
endmodule

module ALU_With_Mem (
  input  [13:0] dest,
  input  CLK,
  output [3:0] ALU_Out
);

  wire not_1_out;
  wire [2:0] multiplexer_1_out;
  wire [3:0] bit_extender_1_out, multiplexer_2_out, multiplexer_3_out, n8x4_bit_register_file_1_read_1_data,
       n8x4_bit_register_file_1_read_2_data, ram_1_data;

  Multiplexer #(.width(3), .enable("false")) multiplexer_1 (
    .in0(dest[2:0]), .in1(dest[8:6]), .out(multiplexer_1_out), .sel(dest[12]));
  not not_1 (not_1_out, dest[12]);
  _8x4_bit_Register_File u_8x4_bit_register_file_1 (
    .Read_Addr_2(multiplexer_1_out), .Data_In(multiplexer_2_out),
    .Read_1_Data(n8x4_bit_register_file_1_read_1_data), .Read_Addr_1(dest[5:3]), .Write_Enable(not_1_out),
    .Write_Addr(dest[8:6]), .Read_2_Data(n8x4_bit_register_file_1_read_2_data), .Clock(CLK));
  Multiplexer #(.width(4), .enable("false")) multiplexer_2 (
    .in0(ALU_Out), .in1(ram_1_data), .out(multiplexer_2_out), .sel(dest[11]));
  assign bit_extender_1_out = {{1{dest[2]}}, dest[2:0]};  // Bit_Extender bit_extender_1
  _4_bit_ALU u_4_bit_alu_1 (
    .A(n8x4_bit_register_file_1_read_1_data), .ALU_Out(ALU_Out), .B(multiplexer_3_out), .ALU_Op(dest[10:9]));
  Multiplexer #(.width(4), .enable("false")) multiplexer_3 (
    .in0(n8x4_bit_register_file_1_read_2_data), .in1(bit_extender_1_out), .out(multiplexer_3_out),
    .sel(dest[13]));
  RAM #(.addrWidth(4), .dataWidth(4), .bus("separate")) ram_1 (
    .addr(ALU_Out), .din(n8x4_bit_register_file_1_read_2_data), .data(ram_1_data), .str(dest[12]), .clk(CLK),
    .ld(dest[11]));  // open: sel, clr

  // Other names for the same wires on the sheet: LW = dest[11]

  // Notes on the sheet:
  //   R/I
  //   dest
  //   op
  //   SW
  //   LW
  //   src1
  //   src2
  //   src2
  //   dest
  //   src1
  //   immed data
  //   immed select
  //   ALU op
endmodule

module Control_Logic (
  input  [4:0] OP_In,
  output [1:0] Op_Code,
  output LW_mux,
  output RAM_ld,
  output RAM_str,
  output WE,
  output D2_mux,
  output RA2_mux
);

  wire not_1_out, or_1_out;

  not not_1 (not_1_out, or_1_out);
  or or_1 (or_1_out, OP_In[2], OP_In[3]);
  not not_2 (WE, OP_In[3]);
  Multiplexer #(.width(2), .enable("false")) multiplexer_1 (
    .in0(2'b00), .in1(OP_In[1:0]), .out(Op_Code), .sel(not_1_out));

  assign D2_mux = OP_In[4];
  assign LW_mux = OP_In[2];
  assign RA2_mux = OP_In[3];
  assign RAM_ld = OP_In[2];
  assign RAM_str = OP_In[3];
endmodule

module ALU_with_Mem_and_Control (
  input  [13:0] dest,
  input  CLK,
  output [3:0] ALU_Out
);

  wire control_logic_1_d2_mux, control_logic_1_ra2_mux, control_logic_1_ram_ld, control_logic_1_ram_str,
       control_logic_1_we, LW;
  wire [1:0] OP;
  wire [2:0] multiplexer_1_out;
  wire [3:0] bit_extender_1_out, multiplexer_2_out, multiplexer_3_out, n8x4_bit_register_file_1_read_1_data,
       n8x4_bit_register_file_1_read_2_data, RAM_Do;

  Control_Logic control_logic_1 (
    .D2_mux(control_logic_1_d2_mux), .WE(control_logic_1_we), .RA2_mux(control_logic_1_ra2_mux),
    .Op_Code(OP), .OP_In(dest[13:9]), .LW_mux(LW), .RAM_str(control_logic_1_ram_str),
    .RAM_ld(control_logic_1_ram_ld));
  Multiplexer #(.width(3), .enable("false")) multiplexer_1 (
    .in0(dest[2:0]), .in1(dest[8:6]), .out(multiplexer_1_out), .sel(control_logic_1_ra2_mux));
  Multiplexer #(.width(4), .enable("false")) multiplexer_2 (
    .in0(ALU_Out), .in1(RAM_Do), .out(multiplexer_2_out), .sel(LW));
  _8x4_bit_Register_File u_8x4_bit_register_file_1 (
    .Read_Addr_2(multiplexer_1_out), .Data_In(multiplexer_2_out),
    .Read_1_Data(n8x4_bit_register_file_1_read_1_data), .Read_Addr_1(dest[5:3]),
    .Write_Enable(control_logic_1_we), .Write_Addr(dest[8:6]),
    .Read_2_Data(n8x4_bit_register_file_1_read_2_data), .Clock(CLK));
  assign bit_extender_1_out = {{1{dest[2]}}, dest[2:0]};  // Bit_Extender bit_extender_1
  Multiplexer #(.width(4), .enable("false")) multiplexer_3 (
    .in0(n8x4_bit_register_file_1_read_2_data), .in1(bit_extender_1_out), .out(multiplexer_3_out),
    .sel(control_logic_1_d2_mux));
  _4_bit_ALU u_4_bit_alu_1 (
    .A(n8x4_bit_register_file_1_read_1_data), .ALU_Out(ALU_Out), .B(multiplexer_3_out), .ALU_Op(OP));
  RAM #(.addrWidth(4), .dataWidth(4), .bus("separate")) ram_1 (
    .addr(ALU_Out), .din(n8x4_bit_register_file_1_read_2_data), .data(RAM_Do), .str(control_logic_1_ram_str),
    .clk(CLK), .ld(control_logic_1_ram_ld));  // open: sel, clr

  // Notes on the sheet:
  //   dest
  //   SW
  //   op
  //   R/I
  //   LW
  //   src1
  //   src2
  //   src2
  //   dest
  //   src1
  //   immed data
  //   immed select
endmodule

module Full_CPU (
  input  Reset,
  input  CLK,
  output [3:0] ALU_Out
);

  wire control_logic_1_d2_mux, control_logic_1_ra2_mux, control_logic_1_ram_ld, control_logic_1_ram_str,
       control_logic_1_we, LW;
  wire [1:0] OP;
  wire [2:0] multiplexer_1_out;
  wire [3:0] bit_extender_1_out, multiplexer_2_out, multiplexer_3_out, n8x4_bit_register_file_1_read_1_data,
       n8x4_bit_register_file_1_read_2_data, RAM_Do;
  wire [4:0] adder_1_out, pc_1_dout;
  wire [15:0] Instr__Wrd;

  Adder #(.width(5)) adder_1 (.a(pc_1_dout), .b(5'b00001), .out(adder_1_out));  // open: cin, cout
  PC pc_1 (.Din(adder_1_out), .Reset(Reset), .CLK(CLK), .Dout(pc_1_dout));
  // Probe on pc_1_dout
  // Probe on Instr__Wrd
  RAM #(.addrWidth(5), .dataWidth(16)) ram_1 (.addr(pc_1_dout), .data(Instr__Wrd));  // open: sel, clk, ld, clr
  Control_Logic control_logic_1 (
    .D2_mux(control_logic_1_d2_mux), .WE(control_logic_1_we), .RA2_mux(control_logic_1_ra2_mux),
    .Op_Code(OP), .OP_In(Instr__Wrd[13:9]), .LW_mux(LW), .RAM_str(control_logic_1_ram_str),
    .RAM_ld(control_logic_1_ram_ld));
  Multiplexer #(.width(3), .enable("false")) multiplexer_1 (
    .in0(Instr__Wrd[2:0]), .in1(Instr__Wrd[8:6]), .out(multiplexer_1_out), .sel(control_logic_1_ra2_mux));
  Multiplexer #(.width(4), .enable("false")) multiplexer_2 (
    .in0(ALU_Out), .in1(RAM_Do), .out(multiplexer_2_out), .sel(LW));
  _8x4_bit_Register_File u_8x4_bit_register_file_1 (
    .Read_Addr_2(multiplexer_1_out), .Data_In(multiplexer_2_out),
    .Read_1_Data(n8x4_bit_register_file_1_read_1_data), .Read_Addr_1(Instr__Wrd[5:3]),
    .Write_Enable(control_logic_1_we), .Write_Addr(Instr__Wrd[8:6]),
    .Read_2_Data(n8x4_bit_register_file_1_read_2_data), .Clock(CLK));
  assign bit_extender_1_out = {{1{Instr__Wrd[2]}}, Instr__Wrd[2:0]};  // Bit_Extender bit_extender_1
  Multiplexer #(.width(4), .enable("false")) multiplexer_3 (
    .in0(n8x4_bit_register_file_1_read_2_data), .in1(bit_extender_1_out), .out(multiplexer_3_out),
    .sel(control_logic_1_d2_mux));
  _4_bit_ALU u_4_bit_alu_1 (
    .A(n8x4_bit_register_file_1_read_1_data), .ALU_Out(ALU_Out), .B(multiplexer_3_out), .ALU_Op(OP));
  RAM #(.addrWidth(4), .dataWidth(4), .bus("separate")) ram_2 (
    .addr(ALU_Out), .din(n8x4_bit_register_file_1_read_2_data), .data(RAM_Do), .str(control_logic_1_ram_str),
    .clk(CLK), .ld(control_logic_1_ram_ld));  // open: sel, clr

  // Notes on the sheet:
  //   Instruction RAM
  //   src2
  //   dest
  //   src1
  //   immed data
  //   immed select
  //   Data RAM
endmodule

module PC (
  input  [4:0] Din,
  input  Reset,
  input  CLK,
  output [4:0] Dout
);

  D_Flip_Flop d_ff_1 (.clk(CLK), .D(Din[0]), .Q(Dout[0]), .en(1'b1), .reset(Reset));  // open: Qn, preset
  D_Flip_Flop d_ff_2 (.clk(CLK), .D(Din[1]), .Q(Dout[1]), .en(1'b1), .reset(Reset));  // open: Qn, preset
  D_Flip_Flop d_ff_3 (.clk(CLK), .D(Din[2]), .Q(Dout[2]), .en(1'b1), .reset(Reset));  // open: Qn, preset
  D_Flip_Flop d_ff_4 (.clk(CLK), .D(Din[3]), .Q(Dout[3]), .en(1'b1), .reset(Reset));  // open: Qn, preset
  D_Flip_Flop d_ff_5 (.clk(CLK), .D(Din[4]), .Q(Dout[4]), .en(1'b1), .reset(Reset));  // open: Qn, preset
endmodule
