// Logisim project Main.circ as structural Verilog
module One_bit_comparater (
  input  X,
  input  Y,
  output Out
);

  wire xor_1_out;

  XOR xor_1 (.A(X), .B(Y), .Out(xor_1_out));
  and and_1 (Out, xor_1_out, Y);
endmodule

module Two_bit_comparator (
  input  X1,
  input  X0,
  input  Y1,
  input  Y0,
  output out_5
);

  wire and_1_out, not_1_out, one_bit_comparater_1_out, one_bit_comparater_2_out, xor_1_out;

  One_bit_comparater one_bit_comparater_1 (.X(X1), .Y(Y1), .Out(one_bit_comparater_1_out));
  One_bit_comparater one_bit_comparater_2 (.X(X0), .Y(Y0), .Out(one_bit_comparater_2_out));
  XOR xor_1 (.A(X1), .B(Y1), .Out(xor_1_out));
  not not_1 (not_1_out, xor_1_out);
  and and_1 (and_1_out, one_bit_comparater_2_out, not_1_out);
  or or_1 (out_5, one_bit_comparater_1_out, and_1_out);
endmodule

module XOR (
  input  A,
  input  B,
  output Out
);

  wire and_1_out, and_2_out, not_1_out, not_2_out;

  not not_1 (not_1_out, B);
  not not_2 (not_2_out, A);
  and and_1 (and_1_out, A, not_1_out);
  and and_2 (and_2_out, not_2_out, B);
  or or_1 (Out, and_1_out, and_2_out);
endmodule
