// Logisim project Main.circ as structural Verilog
module SR_latch (
  input  R,
  input  in_2,
  output Q,
  output Q_prime
);

  wire or_1_out, or_2_out;

  or or_1 (or_1_out, R, Q_prime);
  or or_2 (or_2_out, Q, in_2);
  not not_1 (Q, or_1_out);
  not not_2 (Q_prime, or_2_out);
endmodule

module D_latch (
  input  D,
  input  E,
  output Q
);

  wire and_1_out, and_2_out, not_1_out;

  not not_1 (not_1_out, D);
  and and_1 (and_1_out, not_1_out, E);
  and and_2 (and_2_out, D, E);
  SR_latch sr_latch_1 (.R(and_1_out), .in_2(and_2_out), .Q(Q));  // open: Q_prime
endmodule

module D_flip_flop (
  input  D,
  output Q
);

  wire CLK_out, d_latch_1_q, not_1_out;

  Clock CLK (.out(CLK_out));
  D_latch d_latch_1 (.D(D), .E(CLK_out), .Q(d_latch_1_q));
  not not_1 (not_1_out, CLK_out);
  D_latch d_latch_2 (.D(d_latch_1_q), .E(not_1_out), .Q(Q));
endmodule
